# Fritzing sketch schematic (saved by Fritzing 0.9.5d)
stripboards: 1

parts:
  Part1 = Arduino Nano (Rev3.0)
  U1 = L9110 H-bridge module [part_number="L9110 H-bridge"]
  Part2 = FC-03 [chip_label=FC-03]
  Part3 = FC-03 [chip_label=FC-03]
  M2 = DC Motor
  M3 = DC Motor
  J14 = male pin header, 7 pins [form="♂ (male)"]
  J15 = male pin header, 7 pins [form="♂ (male)"]
  J16 = male pin header, 7 pins [form="♂ (male)"]
  J17 = male pin header, 7 pins [form="♂ (male)"]
  J18 = female pin header, 6 pins [form="♀ (female)"]

nets:
  N1: Part1.GND, Part2.pin_2, Part3.pin_2, J14.pin4, J15.pin4, J16.pin4, J17.pin4, J18.pin3
  N2: Part1.D2, Part3.pin_3
  N3: Part1.D3, Part2.pin_3
  N4: Part1.D9, U1.A-IB
  N5: Part1.D10, U1.A-IA
  N6: Part1.D11/MOSI, U1.B-IB
  N7: Part1.D12/MISO, U1.B-IA
  N8: Part1.5V, Part2.pin_1, Part3.pin_1, J14.pin5, J15.pin5, J16.pin5, J17.pin5, J18.pin4
  N9: Part1.A5, J14.pin7, J15.pin7, J16.pin7, J17.pin7, J18.pin6
  N10: Part1.A4, J14.pin6, J15.pin6, J16.pin6, J17.pin6, J18.pin5
  N11: U1.GND, J14.pin3, J15.pin3, J16.pin3, J17.pin3, J18.pin2
  N12: U1.VCC, J14.pin2, J15.pin2, J16.pin2, J17.pin2, J18.pin1
  N13: U1.MOTOR_A-A, M2.pin_2
  N14: U1.MOTOR_A-B, M2.pin_1
  N15: U1.MOTOR_B-A, M3.pin_2
  N16: U1.MOTOR_B-B, M3.pin_1
  N17: J14.pin1, J15.pin1, J16.pin1, J17.pin1

notes:
  GND
  VCC
  SDA
  SCL

custom parts:
  FC-03: FC-03, LM393 IR Speed Sensor Encoder
